// Logisim project cpu2247.circ as structural Verilog: 6 circuits, main circuit main
module main (
);

  wire ALUSRC, Branch, Branch_Ctrl, button_1_out, CLK, clock_1_out, comparator_1_eq, comparator_1_gt,
       comparator_1_lt, Display_WE, Halt, jr, Jump, multiplexer_4_out, not_1_out, or_2_out, Reg_WE, Store;
  wire [1:0] BranchOp;
  wire [2:0] AluOp, rd, RegDataSrc, rs, rt;
  wire [3:0] display_unit_1_digit_0, display_unit_1_digit_1, display_unit_1_digit_2, display_unit_1_digit_3;
  wire [7:0] ALU_Out, Data, imm, multiplexer_1_out, multiplexer_2_out, multiplexer_3_out, PC_1,
       pc_fsm_1_pc_out, REG_rs, REG_rt;
  wire [21:0] rom_1_data;

  Clock clock_1 (.out(clock_1_out));
  or or_1 (CLK, clock_1_out, button_1_out);
  Button button_1 (.out(button_1_out));
  Hex_Digit_Display hex_digit_display_1 (.value(display_unit_1_digit_3));  // open: dp
  Display_Unit display_unit_1 (
    .D_Lo(REG_rt), .D_Hi(REG_rs), .WE(Display_WE), .CLK(CLK), .Digit_0(display_unit_1_digit_0),
    .Digit_1(display_unit_1_digit_1), .Digit_2(display_unit_1_digit_2), .Digit_3(display_unit_1_digit_3));
  Multiplexer #(.select(3), .width(8)) multiplexer_1 (
    .in0(ALU_Out), .in1(imm), .in2(REG_rs), .in3(Data), .in4(PC_1), .out(multiplexer_1_out), .sel(RegDataSrc));  // open: in5, in6, in7, en
  Multiplexer #(.width(8)) multiplexer_2 (.in0(REG_rt), .in1(imm), .out(multiplexer_2_out), .sel(ALUSRC));  // open: en
  Hex_Digit_Display hex_digit_display_2 (.value(display_unit_1_digit_2));  // open: dp
  Hex_Digit_Display hex_digit_display_3 (.value(display_unit_1_digit_1));  // open: dp
  Register_File register_file_1 (
    .REG_rd(multiplexer_1_out), .rd(rd), .Reg_WE(Reg_WE), .rs(rs), .rt(rt), .CLK(CLK), .REG_rs(REG_rs),
    .REG_rt(REG_rt));
  ALU alu_1 (.ALU_A(REG_rs), .ALU_B(multiplexer_2_out), .ALU_Op(AluOp), .ALU_Out(ALU_Out));
  Hex_Digit_Display hex_digit_display_4 (.value(display_unit_1_digit_0));  // open: dp
  LED led_1 (.in(Halt));
  Multiplexer #(.width(8)) multiplexer_3 (.in0(imm), .in1(REG_rs), .out(multiplexer_3_out), .sel(jr));  // open: en
  // Probe on pc_fsm_1_pc_out
  PC_FSM pc_fsm_1 (
    .Halt(Halt), .Offset(imm), .Branch(Branch), .Target(multiplexer_3_out), .Jump(Jump),
    .PC_Out(pc_fsm_1_pc_out), .PC_1_Out(PC_1), .CLK(CLK));
  ROM #(.dataWidth(22)) rom_1 (.addr(pc_fsm_1_pc_out), .data(rom_1_data));  // open: sel
  RAM #(.bus("separate")) ram_1 (
    .addr(ALU_Out), .din(REG_rt), .data(Data), .str(Store), .clk(CLK));  // open: sel, ld, clr
  Comparator comparator_1 (.a(REG_rs), .b(REG_rt), .gt(comparator_1_gt), .eq(comparator_1_eq), .lt(comparator_1_lt));
  Control control_1 (
    .in_1(rom_1_data), .rt(rt), .rs(rs), .rd(rd), .hlt(Halt), .put(Display_WE), .imm(imm), .Reg_WE(Reg_WE),
    .RegDataSrc(RegDataSrc), .AluSRC(ALUSRC), .ALUOp(AluOp), .Store(Store), .jr(jr), .Jump(Jump),
    .Branch_Ctrl(Branch_Ctrl), .BranchOp(BranchOp));
  or or_2 (or_2_out, comparator_1_gt, comparator_1_eq);
  not not_1 (not_1_out, comparator_1_eq);
  Multiplexer #(.select(2)) multiplexer_4 (
    .in0(or_2_out), .in1(comparator_1_eq), .in2(not_1_out), .in3(comparator_1_lt), .out(multiplexer_4_out),
    .sel(BranchOp));  // open: en
  and and_1 (Branch, multiplexer_4_out, Branch_Ctrl, Branch_Ctrl);

  // Notes on the sheet:
  //   HALT
  //   contents of rom_1 (hex, n*v repeats v):
  //   40101 40202 40303 2c0710 24000 2c0710 28000 2c070a 2c000 0 bf000 1c3601 2c0710 1e3601 83700 2e3800
  //   20000 2e3800
endmodule

// Dis Un
module Display_Unit (
  input  [7:0] D_Lo,
  input  [7:0] D_Hi,
  input  WE,
  input  CLK,
  output [3:0] Digit_0,
  output [3:0] Digit_1,
  output [3:0] Digit_2,
  output [3:0] Digit_3
);

  Register #(.width(16)) register_1 (
    .D({D_Hi, D_Lo}), .en(WE), .Q({Digit_3, Digit_2, Digit_1, Digit_0}), .clk(CLK));  // open: clr
endmodule

module ALU (
  input  [7:0] ALU_A,
  input  [7:0] ALU_B,
  input  [2:0] ALU_Op,
  output [7:0] ALU_Out
);

  wire [2:0] bit_extender_1_out, bit_extender_2_out;
  wire [7:0] A___B, A__B, ADD, AND, nB, OR, SUB, XOR;

  // NOT_Gate not_1 has open pins: in=open, out=nB
  Adder adder_1 (.a(ALU_A), .b(ALU_B), .out(ADD));  // open: cin, cout
  Subtractor subtractor_1 (.a(ALU_A), .b(ALU_B), .out(SUB));  // open: bin, bout
  assign AND = ALU_A & ALU_B;  // AND_Gate A_B, 8 bits wide
  // OR_Gate #(.width(8)) A_B_2: pin names not known; wires that end beside it: ALU_A, ALU_B, OR
  assign XOR = ALU_A ^ ALU_B;  // XOR_Gate xor_1, 8 bits wide
  Shifter shifter_1 (.in(ALU_A), .\dist (bit_extender_1_out), .out(A__B));
  Bit_Extender #(.out_width(3)) bit_extender_1 (.in(ALU_B), .out(bit_extender_1_out));
  Shifter #(.shift("lr")) shifter_2 (.in(ALU_A), .\dist (bit_extender_2_out), .out(A___B));
  Bit_Extender #(.out_width(3)) bit_extender_2 (.in(ALU_B), .out(bit_extender_2_out));
  Multiplexer #(.select(3), .width(8)) multiplexer_1 (
    .in0(ADD), .in1(SUB), .in2(AND), .in3(OR), .in4(XOR), .in5(nB), .in6(A__B), .in7(A___B), .out(ALU_Out),
    .sel(ALU_Op));  // open: en
endmodule

module Register_File (
  input  [7:0] REG_rd,
  input  [2:0] rd,
  input  Reg_WE,
  input  [2:0] rs,
  input  [2:0] rt,
  input  CLK,
  output [7:0] REG_rs,
  output [7:0] REG_rt
);

  wire demultiplexer_1_out1, demultiplexer_1_out2, demultiplexer_1_out3, demultiplexer_1_out4,
       demultiplexer_1_out5, demultiplexer_1_out6, demultiplexer_1_out7;
  wire [7:0] register_1_q, register_2_q, register_3_q, register_4_q, register_5_q, register_6_q, register_7_q;

  Demultiplexer #(.select(3)) demultiplexer_1 (
    .out1(demultiplexer_1_out1), .out2(demultiplexer_1_out2), .out3(demultiplexer_1_out3),
    .out4(demultiplexer_1_out4), .out5(demultiplexer_1_out5), .out6(demultiplexer_1_out6),
    .out7(demultiplexer_1_out7), .in(Reg_WE), .sel(rd));  // open: out0, en
  Register register_1 (.D(REG_rd), .en(demultiplexer_1_out1), .Q(register_1_q), .clk(CLK));  // open: clr
  Register register_2 (.D(REG_rd), .en(demultiplexer_1_out2), .Q(register_2_q), .clk(CLK));  // open: clr
  Register register_3 (.D(REG_rd), .en(demultiplexer_1_out3), .Q(register_3_q), .clk(CLK));  // open: clr
  Register register_4 (.D(REG_rd), .en(demultiplexer_1_out4), .Q(register_4_q), .clk(CLK));  // open: clr
  Register register_5 (.D(REG_rd), .en(demultiplexer_1_out5), .Q(register_5_q), .clk(CLK));  // open: clr
  Register register_6 (.D(REG_rd), .en(demultiplexer_1_out6), .Q(register_6_q), .clk(CLK));  // open: clr
  Register register_7 (.D(REG_rd), .en(demultiplexer_1_out7), .Q(register_7_q), .clk(CLK));  // open: clr
  Multiplexer #(.select(3), .width(8)) multiplexer_1 (
    .in0({8{1'b0}}), .in1(register_1_q), .in2(register_2_q), .in3(register_3_q), .in4(register_4_q),
    .in5(register_5_q), .in6(register_6_q), .in7(register_7_q), .out(REG_rs), .sel(rs));  // open: en
  Multiplexer #(.select(3), .width(8)) multiplexer_2 (
    .in0({8{1'b0}}), .in1(register_1_q), .in2(register_2_q), .in3(register_3_q), .in4(register_4_q),
    .in5(register_5_q), .in6(register_6_q), .in7(register_7_q), .out(REG_rt), .sel(rt));  // open: en
endmodule

module PC_FSM (
  input  Halt,
  input  [7:0] Offset,
  input  Branch,
  input  [7:0] Target,
  input  Jump,
  input  CLK,
  output [7:0] PC_Out,
  output [7:0] PC_1_Out
);

  wire not_1_out;
  wire [7:0] multiplexer_1_out, multiplexer_2_out;

  Multiplexer #(.width(8)) multiplexer_1 (.in0(8'h1), .in1(Offset), .out(multiplexer_1_out), .sel(Branch));  // open: en
  Adder adder_1 (.a(PC_Out), .b(multiplexer_1_out), .out(PC_1_Out));  // open: cin, cout
  Multiplexer #(.width(8)) multiplexer_2 (
    .in0(PC_1_Out), .in1(Target), .out(multiplexer_2_out), .sel(Jump));  // open: en
  Register PC (.D(multiplexer_2_out), .en(not_1_out), .Q(PC_Out), .clk(CLK));  // open: clr
  // NOT_Gate not_1 has open pins: in=open, out=not_1_out
endmodule

module Control (
  input  [21:0] in_1,
  output [2:0] rt,
  output [2:0] rs,
  output [2:0] rd,
  output hlt,
  output put,
  output Store,
  output [7:0] imm,
  output jr,
  output Jump,
  output [2:0] ALUOp,
  output [1:0] BranchOp,
  output Reg_WE,
  output Branch_Ctrl,
  output [2:0] RegDataSrc,
  output AluSRC
);

  wire add, adi, \and , ani, beq, bge, blt, bne, j, jal, ld, li, mov, \not , \or , or_1_out, or_2_out,
       or_3_out, or_4_out, or_5_out, or_6_out, ori, sbi, shl, shr, sli, sri, sub, undriven, undriven_2,
       undriven_3, \xor , xri;

  Decoder #(.select(5)) decoder_1 (
    .out0(hlt), .out1(put), .out2(li), .out3(mov), .out4(ld), .out5(Store), .out6(add), .out7(sub),
    .out8(\and ), .out9(\or ), .out10(\xor ), .out11(\not ), .out12(shl), .out13(shr), .out14(adi),
    .out15(sbi), .out16(ani), .out17(ori), .out18(xri), .out19(sli), .out20(sri), .out21(j), .out22(jal),
    .out23(jr), .out24(blt), .out25(bge), .out26(beq), .out27(bne), .sel(in_1[21:17]));  // open: out28, out29, out30, out31, en
  or or_1 (or_1_out, sub, sbi);
  buf or_2 (or_2_out, undriven);  // OR_Gate
  or or_3 (or_3_out, undriven, undriven_2);
  or or_4 (or_4_out, undriven_2, undriven_3);
  buf or_5 (or_5_out, undriven_3);  // OR_Gate
  or or_6 (or_6_out, shr, sri);
  Priority_Encoder priority_encoder_1 (
    .in0(1'b1), .in1(or_1_out), .in2(or_2_out), .in3(or_3_out), .in4(or_4_out), .in5(\not ), .in6(or_5_out),
    .in7(or_6_out), .out(ALUOp));  // open: en_in, gs, en_out
  Priority_Encoder priority_encoder_2 (
    .in0(1'b1), .in1(li), .in2(mov), .in3(ld), .in4(jal), .out(RegDataSrc));  // open: in5, in6, in7, en_in, gs, en_out
  or or_7 (Reg_WE, li, mov, ld, add, sub, \and , \or , \xor , \not , shl, shr, adi, sbi, ani, ori, xri, sli, sri, jal);
  or or_8 (AluSRC, ori, Store, adi, sbi, ani, xri, sli, sri, li, ld);
  or or_9 (Jump, j, jal, jr);
  Priority_Encoder #(.select(2)) priority_encoder_3 (
    .in0(1'b1), .in1(beq), .in2(bne), .in3(blt), .out(BranchOp));  // open: gs, en_out, en_in
  or or_10 (Branch_Ctrl, bge, beq, bne, blt);

  assign imm = in_1[7:0];
  assign rd = in_1[10:8];
  assign rs = in_1[13:11];
  assign rt = in_1[16:14];

  // Other names for the same wires on the sheet: opcode[4:0] = in_1[21:17]; st = Store
endmodule
